// Logisim project Final_project  (2).circ as structural Verilog: 24 circuits, main circuit main
module main (
  input  A0,
  input  A1,
  input  A2,
  input  A3,
  input  SA,
  input  B0,
  input  B1,
  input  B2,
  input  B3,
  input  SB,
  input  in_11,
  input  in_12
);

  wire bcd_to_seven_segment_1_a_2, bcd_to_seven_segment_1_b_2, bcd_to_seven_segment_1_c_2,
       bcd_to_seven_segment_1_d_2, bcd_to_seven_segment_1_e, bcd_to_seven_segment_1_f,
       bcd_to_seven_segment_1_g, bcd_to_seven_segment_2_a_2, bcd_to_seven_segment_2_b_2,
       bcd_to_seven_segment_2_c_2, bcd_to_seven_segment_2_d_2, bcd_to_seven_segment_2_e,
       bcd_to_seven_segment_2_f, bcd_to_seven_segment_2_g, bcd_to_seven_segment_3_a_2,
       bcd_to_seven_segment_3_b_2, bcd_to_seven_segment_3_c_2, bcd_to_seven_segment_3_d_2,
       bcd_to_seven_segment_3_e, bcd_to_seven_segment_3_f, bcd_to_seven_segment_3_g, binary_to_bcd_1_p0,
       binary_to_bcd_1_p1, binary_to_bcd_1_p2, binary_to_bcd_1_p3, binary_to_bcd_1_p4, binary_to_bcd_1_p5,
       binary_to_bcd_1_p6, binary_to_bcd_1_p7, binary_to_bcd_1_p8, binary_to_bcd_1_p9,
       div_by_zero_to_7seg_1_a, div_by_zero_to_7seg_1_b, div_by_zero_to_7seg_1_c, div_by_zero_to_7seg_1_d,
       div_by_zero_to_7seg_1_e, div_by_zero_to_7seg_1_f, div_by_zero_to_7seg_1_g, div_by_zero_to_7seg_2_a,
       div_by_zero_to_7seg_2_b, div_by_zero_to_7seg_2_c, div_by_zero_to_7seg_2_d, div_by_zero_to_7seg_2_e,
       div_by_zero_to_7seg_2_f, div_by_zero_to_7seg_2_g, div_by_zero_to_7seg_3_a, div_by_zero_to_7seg_3_b,
       div_by_zero_to_7seg_3_c, div_by_zero_to_7seg_3_d, div_by_zero_to_7seg_3_e, div_by_zero_to_7seg_3_f,
       div_by_zero_to_7seg_3_g, operations_1_division_by_zero, operations_1_n0, operations_1_n1,
       operations_1_n2, operations_1_n3, operations_1_n4, operations_1_n5, operations_1_n6, operations_1_n7,
       operations_1_sign, operations_1_zero_ans;

  LED Zero_flag (.in(operations_1_zero_ans));
  Operations operations_1 (
    .in_1(in_11), .in_2(in_12), .BS(SB), .B3(B3), .B2(B2), .B1(B1), .B0(B0), .AS(SA), .A3(A3), .A2(A2),
    .A1(A1), .A0(A0), .division_by_zero(operations_1_division_by_zero), .sign(operations_1_sign),
    .N7(operations_1_n7), .N6(operations_1_n6), .N5(operations_1_n5), .N4(operations_1_n4),
    .N3(operations_1_n3), .N2(operations_1_n2), .N1(operations_1_n1), .N0(operations_1_n0),
    .zero_ans(operations_1_zero_ans));
  LED div__by_zero (.in(operations_1_division_by_zero));
  LED Sign_flag (.in(operations_1_sign));
  binary_to_BCD binary_to_bcd_1 (
    .B0(operations_1_n0), .B1(operations_1_n1), .B2(operations_1_n2), .B3(operations_1_n3),
    .B4(operations_1_n4), .B5(operations_1_n5), .B6(operations_1_n6), .B7(operations_1_n7),
    .P0(binary_to_bcd_1_p0), .P1(binary_to_bcd_1_p1), .P2(binary_to_bcd_1_p2), .P3(binary_to_bcd_1_p3),
    .P4(binary_to_bcd_1_p4), .P5(binary_to_bcd_1_p5), .P6(binary_to_bcd_1_p6), .P7(binary_to_bcd_1_p7),
    .P8(binary_to_bcd_1_p8), .P9(binary_to_bcd_1_p9));
  BCD_to_seven_segment bcd_to_seven_segment_1 (
    .A(binary_to_bcd_1_p3), .B(binary_to_bcd_1_p2), .C(binary_to_bcd_1_p1), .D(binary_to_bcd_1_p0),
    .a_2(bcd_to_seven_segment_1_a_2), .b_2(bcd_to_seven_segment_1_b_2), .c_2(bcd_to_seven_segment_1_c_2),
    .d_2(bcd_to_seven_segment_1_d_2), .e(bcd_to_seven_segment_1_e), .f(bcd_to_seven_segment_1_f),
    .g(bcd_to_seven_segment_1_g));
  BCD_to_seven_segment bcd_to_seven_segment_2 (
    .A(binary_to_bcd_1_p7), .B(binary_to_bcd_1_p6), .C(binary_to_bcd_1_p5), .D(binary_to_bcd_1_p4),
    .a_2(bcd_to_seven_segment_2_a_2), .b_2(bcd_to_seven_segment_2_b_2), .c_2(bcd_to_seven_segment_2_c_2),
    .d_2(bcd_to_seven_segment_2_d_2), .e(bcd_to_seven_segment_2_e), .f(bcd_to_seven_segment_2_f),
    .g(bcd_to_seven_segment_2_g));
  BCD_to_seven_segment bcd_to_seven_segment_3 (
    .A(1'b0), .B(1'b0), .C(binary_to_bcd_1_p9), .D(binary_to_bcd_1_p8), .a_2(bcd_to_seven_segment_3_a_2),
    .b_2(bcd_to_seven_segment_3_b_2), .c_2(bcd_to_seven_segment_3_c_2), .d_2(bcd_to_seven_segment_3_d_2),
    .e(bcd_to_seven_segment_3_e), .f(bcd_to_seven_segment_3_f), .g(bcd_to_seven_segment_3_g));
  Div_by_zero_TO_7SEG div_by_zero_to_7seg_1 (
    .in_1(bcd_to_seven_segment_3_a_2), .in_2(bcd_to_seven_segment_3_b_2), .in_3(bcd_to_seven_segment_3_c_2),
    .in_4(bcd_to_seven_segment_3_d_2), .in_5(bcd_to_seven_segment_3_e), .in_6(bcd_to_seven_segment_3_f),
    .in_7(bcd_to_seven_segment_3_g), .in_8(operations_1_division_by_zero), .a(div_by_zero_to_7seg_1_a),
    .b(div_by_zero_to_7seg_1_b), .c(div_by_zero_to_7seg_1_c), .d(div_by_zero_to_7seg_1_d),
    .e(div_by_zero_to_7seg_1_e), .f(div_by_zero_to_7seg_1_f), .g(div_by_zero_to_7seg_1_g));
  _7_Segment_Display u_7_segment_display_1 (
    .g(div_by_zero_to_7seg_1_g), .f(div_by_zero_to_7seg_1_f), .a(div_by_zero_to_7seg_1_a),
    .b(div_by_zero_to_7seg_1_b), .e(div_by_zero_to_7seg_1_e), .d(div_by_zero_to_7seg_1_d),
    .c(div_by_zero_to_7seg_1_c));  // open: dp
  Div_by_zero_TO_7SEG div_by_zero_to_7seg_2 (
    .in_1(bcd_to_seven_segment_1_a_2), .in_2(bcd_to_seven_segment_1_b_2), .in_3(bcd_to_seven_segment_1_c_2),
    .in_4(bcd_to_seven_segment_1_d_2), .in_5(bcd_to_seven_segment_1_e), .in_6(bcd_to_seven_segment_1_f),
    .in_7(bcd_to_seven_segment_1_g), .in_8(operations_1_division_by_zero), .a(div_by_zero_to_7seg_2_a),
    .b(div_by_zero_to_7seg_2_b), .c(div_by_zero_to_7seg_2_c), .d(div_by_zero_to_7seg_2_d),
    .e(div_by_zero_to_7seg_2_e), .f(div_by_zero_to_7seg_2_f), .g(div_by_zero_to_7seg_2_g));
  Div_by_zero_TO_7SEG div_by_zero_to_7seg_3 (
    .in_1(bcd_to_seven_segment_2_a_2), .in_2(bcd_to_seven_segment_2_b_2), .in_3(bcd_to_seven_segment_2_c_2),
    .in_4(bcd_to_seven_segment_2_d_2), .in_5(bcd_to_seven_segment_2_e), .in_6(bcd_to_seven_segment_2_f),
    .in_7(bcd_to_seven_segment_2_g), .in_8(operations_1_division_by_zero), .a(div_by_zero_to_7seg_3_a),
    .b(div_by_zero_to_7seg_3_b), .c(div_by_zero_to_7seg_3_c), .d(div_by_zero_to_7seg_3_d),
    .e(div_by_zero_to_7seg_3_e), .f(div_by_zero_to_7seg_3_f), .g(div_by_zero_to_7seg_3_g));
  _7_Segment_Display u_7_segment_display_2 (
    .g(div_by_zero_to_7seg_2_g), .f(div_by_zero_to_7seg_2_f), .a(div_by_zero_to_7seg_2_a),
    .b(div_by_zero_to_7seg_2_b), .e(div_by_zero_to_7seg_2_e), .d(div_by_zero_to_7seg_2_d),
    .c(div_by_zero_to_7seg_2_c));  // open: dp
  _7_Segment_Display u_7_segment_display_3 (
    .g(div_by_zero_to_7seg_3_g), .f(div_by_zero_to_7seg_3_f), .a(div_by_zero_to_7seg_3_a),
    .b(div_by_zero_to_7seg_3_b), .e(div_by_zero_to_7seg_3_e), .d(div_by_zero_to_7seg_3_d),
    .c(div_by_zero_to_7seg_3_c));  // open: dp

  // Notes on the sheet:
  //   00 Addition
  //   10 Substraction
  //   01 multiplication
  //   11 Divison
  //   0 +ve  1 -ve
endmodule

// HA
module Half_adder (
  input  A,
  input  B,
  output S,
  output C
);

  xor xor_1 (S, A, B);
  and and_1 (C, A, B);
endmodule

// FA
module Full_adder (
  input  A,
  input  B,
  input  Cin,
  output Sum,
  output Cout
);

  wire half_adder_1_c, half_adder_1_s, half_adder_2_c;

  Half_adder half_adder_1 (.A(A), .B(B), .S(half_adder_1_s), .C(half_adder_1_c));
  Half_adder half_adder_2 (.A(half_adder_1_s), .B(Cin), .S(Sum), .C(half_adder_2_c));
  or or_1 (Cout, half_adder_1_c, half_adder_2_c);
endmodule

// 7 segment
module _7_Segment (
  input  A,
  input  B,
  input  C,
  input  D,
  output a_2,
  output b_2,
  output c_2,
  output d_2,
  output e,
  output f,
  output g
);

  wire and_1_out, and_2_out, and_3_out, and_4_out, and_5_out, and_6_out, and_7_out, and_8_out, and_9_out,
       not_1_out, not_2_out, not_3_out, not_4_out, or_1_out, or_2_out, or_3_out, or_4_out, or_9_out,
       or_10_out, or_11_out, or_12_out, or_13_out, or_14_out, or_16_out;

  not not_1 (not_1_out, A);
  not not_2 (not_2_out, B);
  not not_3 (not_3_out, C);
  not not_4 (not_4_out, D);
  and and_1 (and_1_out, B, D);
  and and_2 (and_2_out, not_2_out, not_4_out);
  and and_3 (and_3_out, C, D);
  and and_4 (and_4_out, not_3_out, not_4_out);
  and and_5 (and_5_out, C, not_4_out);
  and and_6 (and_6_out, not_2_out, C);
  and and_7 (and_7_out, B, not_3_out);
  and and_8 (and_8_out, B, not_4_out);
  and and_9 (and_9_out, D, and_7_out);
  or or_1 (or_1_out, and_1_out, and_2_out);
  or or_2 (or_2_out, or_1_out, A);
  or or_3 (or_3_out, not_2_out, and_4_out);
  or or_4 (or_4_out, B, not_3_out);
  or or_5 (e, and_5_out, and_2_out);
  or or_6 (a_2, or_2_out, C);
  or or_7 (b_2, and_3_out, or_3_out);
  or or_8 (c_2, or_4_out, D);
  or or_9 (or_9_out, and_4_out, and_8_out);
  or or_10 (or_10_out, A, and_2_out);
  or or_11 (or_11_out, and_5_out, and_7_out);
  or or_12 (or_12_out, or_10_out, and_5_out);
  or or_13 (or_13_out, or_9_out, and_7_out);
  or or_14 (or_14_out, or_12_out, and_6_out);
  or or_15 (f, or_13_out, A);
  or or_16 (or_16_out, or_11_out, A);
  or or_17 (d_2, or_14_out, and_9_out);
  or or_18 (g, or_16_out, and_6_out);
endmodule

// Controlled +/-
module Controlled_series_adder (
  input  S,
  input  A0,
  input  B0,
  input  A1,
  input  B1,
  input  A2,
  input  B2,
  input  A3,
  input  B3,
  output S0,
  output S1,
  output S2,
  output S3,
  output C4
);

  wire full_adder_1_cout, full_adder_2_cout, full_adder_3_cout, xor_1_out, xor_2_out, xor_3_out, xor_4_out;

  xor xor_1 (xor_1_out, S, B0);
  xor xor_2 (xor_2_out, S, B1);
  xor xor_3 (xor_3_out, S, B2);
  xor xor_4 (xor_4_out, S, B3);
  Full_adder full_adder_1 (.A(A0), .B(xor_1_out), .Cin(S), .Sum(S0), .Cout(full_adder_1_cout));
  Full_adder full_adder_2 (.A(A1), .B(xor_2_out), .Cin(full_adder_1_cout), .Sum(S1), .Cout(full_adder_2_cout));
  Full_adder full_adder_3 (.A(A2), .B(xor_3_out), .Cin(full_adder_2_cout), .Sum(S2), .Cout(full_adder_3_cout));
  Full_adder full_adder_4 (.A(A3), .B(xor_4_out), .Cin(full_adder_3_cout), .Sum(S3), .Cout(C4));
endmodule

module Addition (
  input  A0,
  input  A1,
  input  A2,
  input  A3,
  input  AS4,
  input  B0,
  input  B1,
  input  B2,
  input  B3,
  input  BS4,
  output S0,
  output out_12,
  output out_13,
  output out_14,
  output S4,
  output sign
);

  wire controlled_series_adder_1_c4, controlled_series_adder_1_s0, controlled_series_adder_1_s1,
       controlled_series_adder_1_s2, controlled_series_adder_1_s3, controlled_series_adder_2_c4,
       controlled_series_adder_2_s0, controlled_series_adder_2_s1, controlled_series_adder_2_s2,
       controlled_series_adder_2_s3, not_1_out, switch_inputs_1_out_11, switch_inputs_1_out_12,
       switch_inputs_1_out_13, switch_inputs_1_out_14, switch_inputs_1_out_15, switch_inputs_1_out_16,
       switch_inputs_1_out_17, switch_inputs_1_out_18, xor_1_out;

  switch_inputs switch_inputs_1 (
    .A0(A0), .A1(A1), .A2(A2), .A3(A3), .AS4(AS4), .B0(B0), .B1(B1), .B2(B2), .B3(B3), .BS4(BS4),
    .out_11(switch_inputs_1_out_11), .out_12(switch_inputs_1_out_12), .out_13(switch_inputs_1_out_13),
    .out_14(switch_inputs_1_out_14), .out_15(switch_inputs_1_out_15), .out_16(switch_inputs_1_out_16),
    .out_17(switch_inputs_1_out_17), .out_18(switch_inputs_1_out_18));
  xor xor_1 (xor_1_out, AS4, BS4);
  Controlled_series_adder controlled_series_adder_1 (
    .S(xor_1_out), .A0(switch_inputs_1_out_11), .B0(switch_inputs_1_out_15), .A1(switch_inputs_1_out_12),
    .B1(switch_inputs_1_out_16), .A2(switch_inputs_1_out_13), .B2(switch_inputs_1_out_17),
    .A3(switch_inputs_1_out_14), .B3(switch_inputs_1_out_18), .S0(controlled_series_adder_1_s0),
    .S1(controlled_series_adder_1_s1), .S2(controlled_series_adder_1_s2), .S3(controlled_series_adder_1_s3),
    .C4(controlled_series_adder_1_c4));
  not not_1 (not_1_out, controlled_series_adder_1_c4);
  Addition_Sign addition_sign_1 (
    .Xor_of_2_signs(xor_1_out), .Sign_of__input_2(BS4),
    .Carry_out_of_1st_Adder(controlled_series_adder_1_c4), .out_4(sign));
  Controlled_series_adder controlled_series_adder_2 (
    .S(not_1_out), .A0(1'b0), .B0(controlled_series_adder_1_s0), .A1(1'b0),
    .B1(controlled_series_adder_1_s1), .A2(1'b0), .B2(controlled_series_adder_1_s2), .A3(1'b0),
    .B3(controlled_series_adder_1_s3), .S0(controlled_series_adder_2_s0), .S1(controlled_series_adder_2_s1),
    .S2(controlled_series_adder_2_s2), .S3(controlled_series_adder_2_s3), .C4(controlled_series_adder_2_c4));
  output_switch output_switch_1 (
    .A0(controlled_series_adder_1_s0), .A1(controlled_series_adder_1_s1), .A2(controlled_series_adder_1_s2),
    .A3(controlled_series_adder_1_s3), .A4(controlled_series_adder_1_c4), .S0(controlled_series_adder_2_s0),
    .S1(controlled_series_adder_2_s1), .S2(controlled_series_adder_2_s2), .S3(controlled_series_adder_2_s3),
    .S4(controlled_series_adder_2_c4), .C(xor_1_out), .out_12(S0), .out_13(out_12), .out_14(out_13),
    .out_15(out_14), .out_16(S4));
endmodule

// +ve first
module switch_inputs (
  input  A0,
  input  A1,
  input  A2,
  input  A3,
  input  AS4,
  input  B0,
  input  B1,
  input  B2,
  input  B3,
  input  BS4,
  output out_11,
  output out_12,
  output out_13,
  output out_14,
  output out_15,
  output out_16,
  output out_17,
  output out_18
);

  wire and_1_out, not_1_out, not_2_out;

  and and_1 (and_1_out, not_1_out, AS4);
  not not_1 (not_1_out, BS4);
  not not_2 (not_2_out, and_1_out);
  _2___1_MUX_east u_2_1_mux_east_1 (.in_1(A0), .in_2(B0), .in_3(and_1_out), .out_4(out_11));
  _2___1_MUX_east u_2_1_mux_east_2 (.in_1(A1), .in_2(B1), .in_3(and_1_out), .out_4(out_12));
  _2___1_MUX_east u_2_1_mux_east_3 (.in_1(A2), .in_2(B2), .in_3(and_1_out), .out_4(out_13));
  _2___1_MUX_east u_2_1_mux_east_4 (.in_1(A3), .in_2(B3), .in_3(and_1_out), .out_4(out_14));
  _2___1_MUX_east u_2_1_mux_east_5 (.in_1(A0), .in_2(B0), .in_3(not_2_out), .out_4(out_15));
  _2___1_MUX_east u_2_1_mux_east_6 (.in_1(A1), .in_2(B1), .in_3(not_2_out), .out_4(out_16));
  _2___1_MUX_east u_2_1_mux_east_7 (.in_1(A2), .in_2(B2), .in_3(not_2_out), .out_4(out_17));
  _2___1_MUX_east u_2_1_mux_east_8 (.in_1(A3), .in_2(B3), .in_3(not_2_out), .out_4(out_18));
endmodule

module output_switch (
  input  A0,
  input  A1,
  input  A2,
  input  A3,
  input  A4,
  input  S0,
  input  S1,
  input  S2,
  input  S3,
  input  S4,
  input  C,
  output out_12,
  output out_13,
  output out_14,
  output out_15,
  output out_16
);

  _2___1_MUX_east u_2_1_mux_east_1 (.in_1(A0), .in_2(S0), .in_3(C), .out_4(out_12));
  _2___1_MUX_east u_2_1_mux_east_2 (.in_1(A1), .in_2(S1), .in_3(C), .out_4(out_13));
  _2___1_MUX_east u_2_1_mux_east_3 (.in_1(A2), .in_2(S2), .in_3(C), .out_4(out_14));
  _2___1_MUX_east u_2_1_mux_east_4 (.in_1(A3), .in_2(S3), .in_3(C), .out_4(out_15));
  _2___1_MUX_east u_2_1_mux_east_5 (.in_1(A4), .in_2(S4), .in_3(C), .out_4(out_16));
endmodule

// Sign
module Addition_Sign (
  input  Xor_of_2_signs,
  input  Sign_of__input_2,
  input  Carry_out_of_1st_Adder,
  output out_4
);

  wire and_1_out, and_2_out, not_1_out, not_2_out;

  not not_1 (not_1_out, Xor_of_2_signs);
  not not_2 (not_2_out, Carry_out_of_1st_Adder);
  and and_1 (and_1_out, not_1_out, Sign_of__input_2);
  and and_2 (and_2_out, Xor_of_2_signs, not_2_out);
  or or_1 (out_4, and_1_out, and_2_out);
endmodule

module Subtractor (
  input  A0,
  input  A1,
  input  A2,
  input  A3,
  input  AS4,
  input  B0,
  input  B1,
  input  B2,
  input  B3,
  input  BS4,
  output out_11,
  output out_12,
  output out_13,
  output out_14,
  output out_15,
  output out_16
);

  wire controlled_series_adder_1_c4, controlled_series_adder_1_s0, controlled_series_adder_1_s1,
       controlled_series_adder_1_s2, controlled_series_adder_1_s3, controlled_series_adder_2_c4,
       controlled_series_adder_2_s0, controlled_series_adder_2_s1, controlled_series_adder_2_s2,
       controlled_series_adder_2_s3, not_1_out, switch_inputs_1_out_11, switch_inputs_1_out_12,
       switch_inputs_1_out_13, switch_inputs_1_out_14, switch_inputs_1_out_15, switch_inputs_1_out_16,
       switch_inputs_1_out_17, switch_inputs_1_out_18, xnor_1_out;

  switch_inputs switch_inputs_1 (
    .A0(A0), .A1(A1), .A2(A2), .A3(A3), .AS4(AS4), .B0(B0), .B1(B1), .B2(B2), .B3(B3), .BS4(BS4),
    .out_11(switch_inputs_1_out_11), .out_12(switch_inputs_1_out_12), .out_13(switch_inputs_1_out_13),
    .out_14(switch_inputs_1_out_14), .out_15(switch_inputs_1_out_15), .out_16(switch_inputs_1_out_16),
    .out_17(switch_inputs_1_out_17), .out_18(switch_inputs_1_out_18));
  xnor xnor_1 (xnor_1_out, AS4, BS4);
  Controlled_series_adder controlled_series_adder_1 (
    .S(xnor_1_out), .A0(switch_inputs_1_out_11), .B0(switch_inputs_1_out_15), .A1(switch_inputs_1_out_12),
    .B1(switch_inputs_1_out_16), .A2(switch_inputs_1_out_13), .B2(switch_inputs_1_out_17),
    .A3(switch_inputs_1_out_14), .B3(switch_inputs_1_out_18), .S0(controlled_series_adder_1_s0),
    .S1(controlled_series_adder_1_s1), .S2(controlled_series_adder_1_s2), .S3(controlled_series_adder_1_s3),
    .C4(controlled_series_adder_1_c4));
  not not_1 (not_1_out, controlled_series_adder_1_c4);
  Sub__sign Sign (
    .xNorOf2Signs(xnor_1_out), .SignOfInput2(BS4), .CarryOutOf1stAdder(controlled_series_adder_1_c4),
    .x(out_16));
  Controlled_series_adder controlled_series_adder_2 (
    .S(not_1_out), .A0(1'b0), .B0(controlled_series_adder_1_s0), .A1(1'b0),
    .B1(controlled_series_adder_1_s1), .A2(1'b0), .B2(controlled_series_adder_1_s2), .A3(1'b0),
    .B3(controlled_series_adder_1_s3), .S0(controlled_series_adder_2_s0), .S1(controlled_series_adder_2_s1),
    .S2(controlled_series_adder_2_s2), .S3(controlled_series_adder_2_s3), .C4(controlled_series_adder_2_c4));
  output_switch output_switch_1 (
    .A0(controlled_series_adder_1_s0), .A1(controlled_series_adder_1_s1), .A2(controlled_series_adder_1_s2),
    .A3(controlled_series_adder_1_s3), .A4(controlled_series_adder_1_c4), .S0(controlled_series_adder_2_s0),
    .S1(controlled_series_adder_2_s1), .S2(controlled_series_adder_2_s2), .S3(controlled_series_adder_2_s3),
    .S4(controlled_series_adder_2_c4), .C(xnor_1_out), .out_12(out_11), .out_13(out_12), .out_14(out_13),
    .out_15(out_14), .out_16(out_15));
endmodule

module Sub__sign (
  input  xNorOf2Signs,
  input  SignOfInput2,
  input  CarryOutOf1stAdder,
  output x
);

  wire and_1_out, and_2_out, and_3_out, and_4_out, not_1_out, not_2_out, not_3_out, not_4_out, or_1_out;

  not not_1 (not_1_out, xNorOf2Signs);
  not not_2 (not_2_out, SignOfInput2);
  not not_3 (not_3_out, SignOfInput2);
  not not_4 (not_4_out, CarryOutOf1stAdder);
  and and_1 (and_1_out, not_1_out, not_2_out);
  and and_2 (and_2_out, not_3_out, not_4_out);
  and and_3 (and_3_out, xNorOf2Signs, SignOfInput2);
  and and_4 (and_4_out, and_3_out, CarryOutOf1stAdder);
  or or_1 (or_1_out, and_2_out, and_4_out);
  or or_2 (x, and_1_out, or_1_out);
endmodule

module multiplier (
  input  A3,
  input  A2,
  input  A1,
  input  A0,
  input  A4,
  input  B0,
  input  B1,
  input  B2,
  input  B3,
  input  B4,
  output Sign,
  output C7,
  output C6,
  output C5,
  output C4,
  output C3,
  output C2,
  output C1,
  output C0
);

  wire and_1_out, and_2_out, and_3_out, and_4_out, and_5_out, and_6_out, and_7_out, and_8_out, and_9_out,
       and_10_out, and_11_out, and_12_out, and_13_out, and_14_out, and_15_out, full_adder_2_cout,
       full_adder_3_cout, full_adder_4_cout, full_adder_5_cout, full_adder_5_sum, full_adder_6_cout,
       full_adder_6_sum, full_adder_7_cout, full_adder_7_sum, full_adder_8_cout, full_adder_8_sum,
       full_adder_9_cout, full_adder_10_cout, full_adder_10_sum, full_adder_11_cout, full_adder_11_sum,
       full_adder_12_cout;

  xor xor_1 (Sign, B4, A4);
  and and_1 (and_1_out, B3, A3);
  and and_2 (and_2_out, B3, A2);
  Full_adder full_adder_1 (.A(full_adder_2_cout), .B(full_adder_6_cout), .Cin(and_1_out), .Sum(C6), .Cout(C7));
  Full_adder full_adder_2 (
    .A(full_adder_3_cout), .B(full_adder_6_sum), .Cin(and_2_out), .Sum(C5), .Cout(full_adder_2_cout));
  and and_3 (and_3_out, B3, A1);
  and and_4 (and_4_out, B3, A0);
  Full_adder full_adder_3 (
    .A(full_adder_4_cout), .B(full_adder_5_sum), .Cin(and_3_out), .Sum(C4), .Cout(full_adder_3_cout));
  and and_5 (and_5_out, B2, A3);
  Full_adder full_adder_4 (.A(1'b0), .B(full_adder_7_sum), .Cin(and_4_out), .Sum(C3), .Cout(full_adder_4_cout));
  and and_6 (and_6_out, B2, A2);
  Full_adder full_adder_5 (
    .A(full_adder_7_cout), .B(full_adder_8_sum), .Cin(and_6_out), .Sum(full_adder_5_sum),
    .Cout(full_adder_5_cout));
  Full_adder full_adder_6 (
    .A(full_adder_5_cout), .B(full_adder_8_cout), .Cin(and_5_out), .Sum(full_adder_6_sum),
    .Cout(full_adder_6_cout));
  and and_7 (and_7_out, B2, A0);
  and and_8 (and_8_out, B2, A1);
  Full_adder full_adder_7 (
    .A(full_adder_9_cout), .B(full_adder_10_sum), .Cin(and_8_out), .Sum(full_adder_7_sum),
    .Cout(full_adder_7_cout));
  and and_9 (and_9_out, A3, B1);
  Full_adder full_adder_8 (
    .A(full_adder_10_cout), .B(1'b0), .Cin(and_9_out), .Sum(full_adder_8_sum), .Cout(full_adder_8_cout));
  Full_adder full_adder_9 (.A(1'b0), .B(full_adder_11_sum), .Cin(and_7_out), .Sum(C2), .Cout(full_adder_9_cout));
  and and_10 (and_10_out, B0, A3);
  and and_11 (and_11_out, B1, A2);
  Full_adder full_adder_10 (
    .A(full_adder_11_cout), .B(and_10_out), .Cin(and_11_out), .Sum(full_adder_10_sum),
    .Cout(full_adder_10_cout));
  and and_12 (and_12_out, B0, A2);
  and and_13 (and_13_out, B1, A0);
  and and_14 (and_14_out, B1, A1);
  Full_adder full_adder_11 (
    .A(full_adder_12_cout), .B(and_12_out), .Cin(and_14_out), .Sum(full_adder_11_sum),
    .Cout(full_adder_11_cout));
  and and_15 (and_15_out, B0, A1);
  Full_adder full_adder_12 (.A(1'b0), .B(and_15_out), .Cin(and_13_out), .Sum(C1), .Cout(full_adder_12_cout));
  and and_16 (C0, B0, A0);
endmodule

module Operations (
  input  in_1,
  input  in_2,
  input  B3,
  input  B2,
  input  B1,
  input  B0,
  input  AS,
  input  A3,
  input  A2,
  input  A1,
  input  A0,
  input  BS,
  output N0,
  output division_by_zero,
  output N1,
  output N2,
  output N3,
  output zero_ans,
  output N4,
  output N5,
  output N6,
  output sign,
  output N7
);

  wire addition_1_out_12, addition_1_out_13, addition_1_out_14, addition_1_s0, addition_1_s4,
       addition_1_sign, div_1_q0, div_1_q1, div_1_q2, div_1_q3, div_1_sign_3, div_1_zero_div,
       multiplier_1_c0, multiplier_1_c1, multiplier_1_c2, multiplier_1_c3, multiplier_1_c4,
       multiplier_1_sign, N0_2_out, N0_3_out, N0_4_out, N0_out, N3_2_out, N3_3_out, N3_4_out, N3_5_out,
       N3_6_out, N3_7_out, n4_1_demux_1_out_4, n4_1_demux_1_out_5, n4_1_demux_1_out_6, n4_1_demux_1_out_7,
       n4_1_demux_2_out_4, n4_1_demux_2_out_5, n4_1_demux_2_out_6, n4_1_demux_2_out_7, n4_1_demux_3_out_4,
       n4_1_demux_3_out_5, n4_1_demux_3_out_6, n4_1_demux_3_out_7, n4_1_demux_4_out_4, n4_1_demux_4_out_5,
       n4_1_demux_4_out_6, n4_1_demux_4_out_7, n4_1_demux_5_out_4, n4_1_demux_5_out_5, n4_1_demux_5_out_6,
       n4_1_demux_5_out_7, n4_1_demux_6_out_4, n4_1_demux_6_out_5, n4_1_demux_6_out_6, n4_1_demux_6_out_7,
       n4_1_demux_7_out_4, n4_1_demux_7_out_5, n4_1_demux_7_out_6, n4_1_demux_7_out_7, n4_1_demux_8_out_4,
       n4_1_demux_8_out_5, n4_1_demux_8_out_6, n4_1_demux_8_out_7, n4_1_demux_9_out_4, n4_1_demux_9_out_5,
       n4_1_demux_9_out_6, n4_1_demux_9_out_7, n4_1_demux_10_out_4, n4_1_demux_10_out_5, n4_1_demux_10_out_6,
       n4_1_demux_10_out_7, N4_out, nand_1_out, nand_2_out, nand_3_out, nand_4_out, nand_5_out, nand_6_out,
       not_1_out, not_2_out, not_3_out, not_4_out, not_5_out, subtractor_1_out_11, subtractor_1_out_12,
       subtractor_1_out_13, subtractor_1_out_14, subtractor_1_out_15, subtractor_1_out_16;

  _4___1_DEMUX u_4_1_demux_1 (
    .in_2(in_1), .in_3(in_2), .in_1(BS), .out_4(n4_1_demux_1_out_4), .out_5(n4_1_demux_1_out_5),
    .out_6(n4_1_demux_1_out_6), .out_7(n4_1_demux_1_out_7));
  _4___1_MUX u_4_1_mux_1 (
    .in_5(in_1), .in_6(in_2), .in_1(1'b0), .in_2(1'b0), .in_3(1'b0), .in_4(div_1_zero_div),
    .out_7(division_by_zero));
  or u_SIGN (sign, div_1_sign_3, N0_2_out);
  or u_N0 (N0_out, subtractor_1_out_16, multiplier_1_sign);
  or N0_2 (N0_2_out, addition_1_sign, N0_out);
  _4___1_DEMUX u_4_1_demux_2 (
    .in_2(in_1), .in_3(in_2), .in_1(B3), .out_4(n4_1_demux_2_out_4), .out_5(n4_1_demux_2_out_5),
    .out_6(n4_1_demux_2_out_6), .out_7(n4_1_demux_2_out_7));
  Div div_1 (
    .sign(n4_1_demux_6_out_7), .A(n4_1_demux_7_out_7), .B(n4_1_demux_8_out_7), .C(n4_1_demux_9_out_7),
    .D(n4_1_demux_10_out_7), .sign_2(n4_1_demux_1_out_7), .E(n4_1_demux_2_out_7), .F(n4_1_demux_3_out_7),
    .G(n4_1_demux_4_out_7), .H(n4_1_demux_5_out_7), .sign_3(div_1_sign_3), .q3(div_1_q3), .Q2(div_1_q2),
    .Q1(div_1_q1), .Q0(div_1_q0), .zero_div(div_1_zero_div));
  _4___1_DEMUX u_4_1_demux_3 (
    .in_2(in_1), .in_3(in_2), .in_1(B2), .out_4(n4_1_demux_3_out_4), .out_5(n4_1_demux_3_out_5),
    .out_6(n4_1_demux_3_out_6), .out_7(n4_1_demux_3_out_7));
  _4___1_DEMUX u_4_1_demux_4 (
    .in_2(in_1), .in_3(in_2), .in_1(B1), .out_4(n4_1_demux_4_out_4), .out_5(n4_1_demux_4_out_5),
    .out_6(n4_1_demux_4_out_6), .out_7(n4_1_demux_4_out_7));
  or u_N4 (N4_out, subtractor_1_out_15, multiplier_1_c4);
  or N4_2 (N4, addition_1_s4, N4_out);
  or u_N3 (N3, div_1_q3, N3_3_out);
  nand nand_1 (nand_1_out, N6, N7);
  _4___1_DEMUX u_4_1_demux_5 (
    .in_2(in_1), .in_3(in_2), .in_1(B0), .out_4(n4_1_demux_5_out_4), .out_5(n4_1_demux_5_out_5),
    .out_6(n4_1_demux_5_out_6), .out_7(n4_1_demux_5_out_7));
  or N3_2 (N3_2_out, subtractor_1_out_14, multiplier_1_c3);
  or N3_3 (N3_3_out, addition_1_out_14, N3_2_out);
  not not_1 (not_1_out, nand_1_out);
  Addition addition_1 (
    .A0(n4_1_demux_10_out_4), .A1(n4_1_demux_9_out_4), .A2(n4_1_demux_8_out_4), .A3(n4_1_demux_7_out_4),
    .AS4(n4_1_demux_6_out_4), .B0(n4_1_demux_5_out_4), .B1(n4_1_demux_4_out_4), .B2(n4_1_demux_3_out_4),
    .B3(n4_1_demux_2_out_4), .BS4(n4_1_demux_1_out_4), .S0(addition_1_s0), .out_12(addition_1_out_12),
    .out_13(addition_1_out_13), .out_14(addition_1_out_14), .S4(addition_1_s4), .sign(addition_1_sign));
  nand nand_2 (nand_2_out, N5, not_1_out);
  _4___1_DEMUX u_4_1_demux_6 (
    .in_2(in_1), .in_3(in_2), .in_1(AS), .out_4(n4_1_demux_6_out_4), .out_5(n4_1_demux_6_out_5),
    .out_6(n4_1_demux_6_out_6), .out_7(n4_1_demux_6_out_7));
  or N3_4 (N3_4_out, addition_1_out_13, N3_5_out);
  or u_N2 (N2, div_1_q2, N3_4_out);
  not not_2 (not_2_out, nand_2_out);
  _4___1_DEMUX u_4_1_demux_7 (
    .in_2(in_1), .in_3(in_2), .in_1(A3), .out_4(n4_1_demux_7_out_4), .out_5(n4_1_demux_7_out_5),
    .out_6(n4_1_demux_7_out_6), .out_7(n4_1_demux_7_out_7));
  or N3_5 (N3_5_out, subtractor_1_out_13, multiplier_1_c2);
  not not_3 (not_3_out, nand_3_out);
  nand nand_3 (nand_3_out, N4, not_2_out);
  or u_N1 (N1, div_1_q1, N3_7_out);
  _4___1_DEMUX u_4_1_demux_8 (
    .in_2(in_1), .in_3(in_2), .in_1(A2), .out_4(n4_1_demux_8_out_4), .out_5(n4_1_demux_8_out_5),
    .out_6(n4_1_demux_8_out_6), .out_7(n4_1_demux_8_out_7));
  nand nand_4 (nand_4_out, N3, not_3_out);
  not not_4 (not_4_out, nand_4_out);
  or N3_6 (N3_6_out, subtractor_1_out_12, multiplier_1_c1);
  or N3_7 (N3_7_out, addition_1_out_12, N3_6_out);
  nand nand_5 (nand_5_out, N2, not_4_out);
  _4___1_DEMUX u_4_1_demux_9 (
    .in_2(in_1), .in_3(in_2), .in_1(A1), .out_4(n4_1_demux_9_out_4), .out_5(n4_1_demux_9_out_5),
    .out_6(n4_1_demux_9_out_6), .out_7(n4_1_demux_9_out_7));
  multiplier multiplier_1 (
    .B0(n4_1_demux_5_out_6), .B1(n4_1_demux_4_out_6), .B2(n4_1_demux_3_out_6), .B3(n4_1_demux_2_out_6),
    .B4(n4_1_demux_1_out_6), .A4(n4_1_demux_6_out_6), .A3(n4_1_demux_7_out_6), .A2(n4_1_demux_8_out_6),
    .A1(n4_1_demux_9_out_6), .A0(n4_1_demux_10_out_6), .Sign(multiplier_1_sign), .C7(N7), .C6(N6), .C5(N5),
    .C4(multiplier_1_c4), .C3(multiplier_1_c3), .C2(multiplier_1_c2), .C1(multiplier_1_c1),
    .C0(multiplier_1_c0));
  Subtractor subtractor_1 (
    .A0(n4_1_demux_10_out_5), .A1(n4_1_demux_9_out_5), .A2(n4_1_demux_8_out_5), .A3(n4_1_demux_7_out_5),
    .AS4(n4_1_demux_6_out_5), .B0(n4_1_demux_5_out_5), .B1(n4_1_demux_4_out_5), .B2(n4_1_demux_3_out_5),
    .B3(n4_1_demux_2_out_5), .BS4(n4_1_demux_1_out_5), .out_11(subtractor_1_out_11),
    .out_12(subtractor_1_out_12), .out_13(subtractor_1_out_13), .out_14(subtractor_1_out_14),
    .out_15(subtractor_1_out_15), .out_16(subtractor_1_out_16));
  not not_5 (not_5_out, nand_5_out);
  nand nand_6 (nand_6_out, N1, not_5_out);
  _4___1_DEMUX u_4_1_demux_10 (
    .in_2(in_1), .in_3(in_2), .in_1(A0), .out_4(n4_1_demux_10_out_4), .out_5(n4_1_demux_10_out_5),
    .out_6(n4_1_demux_10_out_6), .out_7(n4_1_demux_10_out_7));
  or N0_3 (N0_3_out, subtractor_1_out_11, multiplier_1_c0);
  or N0_4 (N0_4_out, addition_1_s0, N0_3_out);
  or N0_5 (N0, div_1_q0, N0_4_out);
  nand nand_7 (zero_ans, N0, nand_6_out);
endmodule

module Div_by_zero_TO_7SEG (
  input  in_1,
  input  in_2,
  input  in_3,
  input  in_4,
  input  in_5,
  input  in_6,
  input  in_7,
  input  in_8,
  output a,
  output b,
  output c,
  output d,
  output e,
  output f,
  output g
);

  wire not_1_out, not_2_out;

  not not_1 (not_1_out, in_8);
  _2___1_MUX_east u_2_1_mux_east_1 (.in_1(in_1), .in_2(in_8), .in_3(in_8), .out_4(a));
  _2___1_MUX_east u_2_1_mux_east_2 (.in_1(in_2), .in_2(not_2_out), .in_3(in_8), .out_4(b));
  not not_2 (not_2_out, in_8);
  _2___1_MUX_east u_2_1_mux_east_3 (.in_1(in_3), .in_2(not_1_out), .in_3(in_8), .out_4(c));
  _2___1_MUX_east u_2_1_mux_east_4 (.in_1(in_4), .in_2(in_8), .in_3(in_8), .out_4(d));
  _2___1_MUX_east u_2_1_mux_east_5 (.in_1(in_6), .in_2(in_8), .in_3(in_8), .out_4(f));
  _2___1_MUX_east u_2_1_mux_east_6 (.in_1(in_7), .in_2(in_8), .in_3(in_8), .out_4(g));
  _2___1_MUX_east u_2_1_mux_east_7 (.in_1(in_5), .in_2(in_8), .in_3(in_8), .out_4(e));
endmodule

module Div (
  input  sign,
  input  A,
  input  B,
  input  C,
  input  D,
  input  sign_2,
  input  E,
  input  F,
  input  G,
  input  H,
  output sign_3,
  output q3,
  output Q2,
  output Q1,
  output Q0,
  output zero_div
);

  wire division_1_out_12, division_1_out_13, division_1_out_14, division_1_out_15, division_1_out_16,
       division_1_out_17, division_1_out_18, division_1_out_19, nor_1_out, nor_2_out, nor_3_out, nor_4_out;

  division division_1 (
    .in_9(1'b0), .B3(E), .in_10(1'b0), .B2(F), .in_11(1'b0), .B1(G), .B0(H), .A3(A), .A2(B), .A1(C), .A0(D),
    .out_12(division_1_out_12), .out_13(division_1_out_13), .out_14(division_1_out_14),
    .out_15(division_1_out_15), .out_16(division_1_out_16), .out_17(division_1_out_17),
    .out_18(division_1_out_18), .out_19(division_1_out_19));
  nor nor_1 (nor_1_out, E, F);
  nor nor_2 (nor_2_out, G, H);
  nor nor_3 (nor_3_out, nor_1_out, nor_1_out);
  nor nor_4 (nor_4_out, nor_2_out, nor_2_out);
  nor nor_5 (zero_div, nor_3_out, nor_4_out);
  xor xor_1 (sign_3, sign, sign_2);
  xor xor_2 (q3, zero_div, division_1_out_12);
  xor xor_3 (Q2, zero_div, division_1_out_13);
  xor xor_4 (Q1, zero_div, division_1_out_14);
  xor xor_5 (Q0, zero_div, division_1_out_15);

  // Notes on the sheet:
  //   digits are arranged from top to bottom as from left to right
  //   integer part
  //   .
  //   Reminder
  //   R3
  //   R2
  //   R1
  //   R0
  //   zero devision error
  //   Q3
endmodule

module division (
  input  B3,
  input  B2,
  input  B1,
  input  B0,
  input  A3,
  input  A2,
  input  A1,
  input  A0,
  input  in_9,
  input  in_10,
  input  in_11,
  output out_12,
  output out_13,
  output out_14,
  output out_15,
  output out_16,
  output out_17,
  output out_18,
  output out_19
);

  wire n2_1_mux_south_1_out_4, n2_1_mux_south_2_out_4, n2_1_mux_south_3_out_4, n2_1_mux_south_4_out_4,
       n2_1_mux_south_5_out_4, n2_1_mux_south_6_out_4, n2_1_mux_south_7_out_4, n2_1_mux_south_8_out_4,
       n2_1_mux_south_10_out_4, subtractor_division_1_borrow, subtractor_division_1_out_5,
       subtractor_division_2_borrow, subtractor_division_2_out_5, subtractor_division_3_borrow,
       subtractor_division_3_out_5, subtractor_division_4_borrow, subtractor_division_4_out_5,
       subtractor_division_5_borrow, subtractor_division_5_out_5, subtractor_division_6_borrow,
       subtractor_division_6_out_5, subtractor_division_7_borrow, subtractor_division_7_out_5,
       subtractor_division_8_borrow, subtractor_division_8_out_5, subtractor_division_9_borrow,
       subtractor_division_9_out_5, subtractor_division_10_borrow, subtractor_division_10_out_5,
       subtractor_division_11_borrow, subtractor_division_11_out_5, subtractor_division_12_borrow,
       subtractor_division_12_out_5, subtractor_division_13_borrow, subtractor_division_13_out_5,
       subtractor_division_14_borrow, subtractor_division_14_out_5, subtractor_division_15_borrow,
       subtractor_division_15_out_5, subtractor_division_16_borrow, subtractor_division_16_out_5;

  not not_1 (out_12, subtractor_division_1_borrow);
  subtractor_division subtractor_division_1 (
    .borrow(subtractor_division_1_borrow), .A(in_9), .B(B3), .out_5(subtractor_division_1_out_5),
    .C(subtractor_division_2_borrow));
  not not_2 (out_13, subtractor_division_4_borrow);
  subtractor_division subtractor_division_2 (
    .borrow(subtractor_division_2_borrow), .A(in_10), .B(B2), .out_5(subtractor_division_2_out_5),
    .C(subtractor_division_3_borrow));
  _2___1_MUX_south u_2_1_mux_south_1 (
    .in_3(subtractor_division_1_borrow), .in_1(subtractor_division_2_out_5), .in_2(in_10),
    .out_4(n2_1_mux_south_1_out_4));
  not not_3 (out_14, subtractor_division_7_borrow);
  subtractor_division subtractor_division_3 (
    .borrow(subtractor_division_3_borrow), .A(in_11), .B(B1), .out_5(subtractor_division_3_out_5),
    .C(subtractor_division_5_borrow));
  _2___1_MUX_south u_2_1_mux_south_2 (
    .in_3(subtractor_division_1_borrow), .in_1(subtractor_division_3_out_5), .in_2(in_11),
    .out_4(n2_1_mux_south_2_out_4));
  subtractor_division subtractor_division_4 (
    .borrow(subtractor_division_4_borrow), .A(n2_1_mux_south_1_out_4), .B(B3),
    .out_5(subtractor_division_4_out_5), .C(subtractor_division_6_borrow));
  _2___1_MUX_south u_2_1_mux_south_3 (
    .in_3(subtractor_division_4_borrow), .in_1(subtractor_division_6_out_5), .in_2(n2_1_mux_south_2_out_4),
    .out_4(n2_1_mux_south_3_out_4));
  not not_4 (out_15, subtractor_division_12_borrow);
  subtractor_division subtractor_division_5 (
    .borrow(subtractor_division_5_borrow), .A(A3), .B(B0), .out_5(subtractor_division_5_out_5), .C(in_11));
  _2___1_MUX_south u_2_1_mux_south_4 (
    .in_3(subtractor_division_1_borrow), .in_1(subtractor_division_5_out_5), .in_2(A3),
    .out_4(n2_1_mux_south_4_out_4));
  subtractor_division subtractor_division_6 (
    .borrow(subtractor_division_6_borrow), .A(n2_1_mux_south_2_out_4), .B(B2),
    .out_5(subtractor_division_6_out_5), .C(subtractor_division_8_borrow));
  _2___1_MUX_south u_2_1_mux_south_5 (
    .in_3(subtractor_division_4_borrow), .in_1(subtractor_division_8_out_5), .in_2(n2_1_mux_south_4_out_4),
    .out_4(n2_1_mux_south_5_out_4));
  subtractor_division subtractor_division_7 (
    .borrow(subtractor_division_7_borrow), .A(n2_1_mux_south_3_out_4), .B(B3),
    .out_5(subtractor_division_7_out_5), .C(subtractor_division_9_borrow));
  subtractor_division subtractor_division_8 (
    .borrow(subtractor_division_8_borrow), .A(n2_1_mux_south_4_out_4), .B(B1),
    .out_5(subtractor_division_8_out_5), .C(subtractor_division_10_borrow));
  subtractor_division subtractor_division_9 (
    .borrow(subtractor_division_9_borrow), .A(n2_1_mux_south_5_out_4), .B(B2),
    .out_5(subtractor_division_9_out_5), .C(subtractor_division_11_borrow));
  _2___1_MUX_south u_2_1_mux_south_6 (
    .in_3(subtractor_division_7_borrow), .in_1(subtractor_division_9_out_5), .in_2(n2_1_mux_south_5_out_4),
    .out_4(n2_1_mux_south_6_out_4));
  subtractor_division subtractor_division_10 (
    .borrow(subtractor_division_10_borrow), .A(A2), .B(B0), .out_5(subtractor_division_10_out_5), .C(in_11));
  _2___1_MUX_south u_2_1_mux_south_7 (
    .in_3(subtractor_division_4_borrow), .in_1(subtractor_division_10_out_5), .in_2(A2),
    .out_4(n2_1_mux_south_7_out_4));
  subtractor_division subtractor_division_11 (
    .borrow(subtractor_division_11_borrow), .A(n2_1_mux_south_7_out_4), .B(B1),
    .out_5(subtractor_division_11_out_5), .C(subtractor_division_13_borrow));
  _2___1_MUX_south u_2_1_mux_south_8 (
    .in_3(subtractor_division_7_borrow), .in_1(subtractor_division_11_out_5), .in_2(n2_1_mux_south_7_out_4),
    .out_4(n2_1_mux_south_8_out_4));
  subtractor_division subtractor_division_12 (
    .borrow(subtractor_division_12_borrow), .A(n2_1_mux_south_6_out_4), .B(B3),
    .out_5(subtractor_division_12_out_5), .C(subtractor_division_14_borrow));
  _2___1_MUX_south u_2_1_mux_south_9 (
    .in_3(subtractor_division_12_borrow), .in_1(subtractor_division_12_out_5), .in_2(n2_1_mux_south_6_out_4),
    .out_4(out_16));
  subtractor_division subtractor_division_13 (
    .borrow(subtractor_division_13_borrow), .A(A1), .B(B0), .out_5(subtractor_division_13_out_5), .C(in_11));
  _2___1_MUX_south u_2_1_mux_south_10 (
    .in_3(subtractor_division_7_borrow), .in_1(subtractor_division_13_out_5), .in_2(A1),
    .out_4(n2_1_mux_south_10_out_4));
  subtractor_division subtractor_division_14 (
    .borrow(subtractor_division_14_borrow), .A(n2_1_mux_south_8_out_4), .B(B2),
    .out_5(subtractor_division_14_out_5), .C(subtractor_division_15_borrow));
  _2___1_MUX_south u_2_1_mux_south_11 (
    .in_3(subtractor_division_12_borrow), .in_1(subtractor_division_14_out_5), .in_2(n2_1_mux_south_8_out_4),
    .out_4(out_17));
  subtractor_division subtractor_division_15 (
    .borrow(subtractor_division_15_borrow), .A(n2_1_mux_south_10_out_4), .B(B1),
    .out_5(subtractor_division_15_out_5), .C(subtractor_division_16_borrow));
  _2___1_MUX_south u_2_1_mux_south_12 (
    .in_3(subtractor_division_12_borrow), .in_1(subtractor_division_15_out_5),
    .in_2(n2_1_mux_south_10_out_4), .out_4(out_18));
  subtractor_division subtractor_division_16 (
    .borrow(subtractor_division_16_borrow), .A(A0), .B(B0), .out_5(subtractor_division_16_out_5), .C(in_11));
  _2___1_MUX_south u_2_1_mux_south_13 (
    .in_3(subtractor_division_12_borrow), .in_1(subtractor_division_16_out_5), .in_2(A0), .out_4(out_19));
endmodule

module subtractor_division (
  input  A,
  input  B,
  input  C,
  output borrow,
  output out_5
);

  wire and_1_out, and_2_out, and_3_out, not_1_out, or_2_out, xor_1_out;

  and and_1 (and_1_out, B, C);
  or or_1 (borrow, and_1_out, or_2_out);
  not not_1 (not_1_out, A);
  and and_2 (and_2_out, B, not_1_out);
  or or_2 (or_2_out, and_2_out, and_3_out);
  and and_3 (and_3_out, C, not_1_out);
  xor xor_1 (xor_1_out, B, C);
  xor xor_2 (out_5, A, xor_1_out);

  // Notes on the sheet:
  //   difference
endmodule

module binary_to_BCD_main (
  input  A3,
  input  A2,
  input  A1,
  input  A0,
  output S3,
  output S2,
  output S1,
  output S0
);

  wire and_1_out, and_2_out, and_3_out, and_4_out, and_5_out, and_6_out, and_7_out, and_8_out, and_9_out,
       and_10_out, and_11_out, and_12_out, and_13_out, not_1_out, not_2_out, not_3_out, not_4_out, not_5_out,
       not_6_out, not_7_out, not_8_out, or_1_out, or_2_out, or_3_out, or_4_out, or_5_out, or_9_out,
       or_10_out, or_11_out;

  or or_1 (or_1_out, A1, A0);
  or or_2 (or_2_out, A2, A1);
  or or_3 (or_3_out, or_2_out, A0);
  not not_1 (not_1_out, A1);
  and and_1 (and_1_out, not_1_out, not_2_out);
  not not_2 (not_2_out, A0);
  not not_3 (not_3_out, A0);
  or or_4 (or_4_out, not_3_out, A2);
  or or_5 (or_5_out, A0, not_4_out);
  not not_4 (not_4_out, A2);
  not not_5 (not_5_out, A3);
  and and_2 (and_2_out, not_5_out, not_6_out);
  not not_6 (not_6_out, A2);
  and and_3 (and_3_out, A2, A1);
  not not_7 (not_7_out, A0);
  and and_4 (and_4_out, A3, not_8_out);
  not not_8 (not_8_out, A0);
  and and_5 (and_5_out, A3, A1);
  and and_6 (and_6_out, A3, A2);
  and and_7 (and_7_out, or_1_out, A2);
  or or_6 (S3, and_7_out, A3);
  and and_8 (and_8_out, or_3_out, A3);
  or or_7 (S2, and_8_out, and_9_out);
  and and_9 (and_9_out, A2, and_1_out);
  and and_10 (and_10_out, or_4_out, A3);
  and and_11 (and_11_out, or_5_out, A1);
  and and_12 (and_12_out, and_2_out, A0);
  and and_13 (and_13_out, and_3_out, not_7_out);
  or or_8 (S1, and_10_out, and_11_out);
  or or_9 (or_9_out, and_5_out, and_6_out);
  or or_10 (or_10_out, and_13_out, or_11_out);
  or or_11 (or_11_out, and_4_out, or_9_out);
  or or_12 (S0, and_12_out, or_10_out);
endmodule

module binary_to_BCD (
  input  B0,
  input  B1,
  input  B2,
  input  B3,
  input  B4,
  input  B5,
  input  B6,
  input  B7,
  output P0,
  output P1,
  output P2,
  output P3,
  output P4,
  output P5,
  output P6,
  output P7,
  output P8,
  output P9
);

  wire binary_to_bcd_main_1_s0, binary_to_bcd_main_1_s1, binary_to_bcd_main_1_s2, binary_to_bcd_main_1_s3,
       binary_to_bcd_main_2_s0, binary_to_bcd_main_2_s1, binary_to_bcd_main_2_s2, binary_to_bcd_main_2_s3,
       binary_to_bcd_main_3_s0, binary_to_bcd_main_3_s1, binary_to_bcd_main_3_s2, binary_to_bcd_main_3_s3,
       binary_to_bcd_main_5_s0, binary_to_bcd_main_5_s1, binary_to_bcd_main_5_s2, binary_to_bcd_main_5_s3,
       binary_to_bcd_main_6_s0, binary_to_bcd_main_6_s1, binary_to_bcd_main_6_s2;

  binary_to_BCD_main binary_to_bcd_main_1 (
    .A3(1'b0), .A2(B7), .A1(B6), .A0(B5), .S3(binary_to_bcd_main_1_s3), .S2(binary_to_bcd_main_1_s2),
    .S1(binary_to_bcd_main_1_s1), .S0(binary_to_bcd_main_1_s0));
  binary_to_BCD_main binary_to_bcd_main_2 (
    .A3(binary_to_bcd_main_1_s2), .A2(binary_to_bcd_main_1_s1), .A1(binary_to_bcd_main_1_s0), .A0(B4),
    .S3(binary_to_bcd_main_2_s3), .S2(binary_to_bcd_main_2_s2), .S1(binary_to_bcd_main_2_s1),
    .S0(binary_to_bcd_main_2_s0));
  binary_to_BCD_main binary_to_bcd_main_3 (
    .A3(binary_to_bcd_main_2_s2), .A2(binary_to_bcd_main_2_s1), .A1(binary_to_bcd_main_2_s0), .A0(B3),
    .S3(binary_to_bcd_main_3_s3), .S2(binary_to_bcd_main_3_s2), .S1(binary_to_bcd_main_3_s1),
    .S0(binary_to_bcd_main_3_s0));
  binary_to_BCD_main binary_to_bcd_main_4 (
    .A3(binary_to_bcd_main_5_s2), .A2(binary_to_bcd_main_5_s1), .A1(binary_to_bcd_main_5_s0), .A0(B1),
    .S3(P4), .S2(P3), .S1(P2), .S0(P1));
  binary_to_BCD_main binary_to_bcd_main_5 (
    .A3(binary_to_bcd_main_3_s2), .A2(binary_to_bcd_main_3_s1), .A1(binary_to_bcd_main_3_s0), .A0(B2),
    .S3(binary_to_bcd_main_5_s3), .S2(binary_to_bcd_main_5_s2), .S1(binary_to_bcd_main_5_s1),
    .S0(binary_to_bcd_main_5_s0));
  binary_to_BCD_main binary_to_bcd_main_6 (
    .A3(1'b0), .A2(binary_to_bcd_main_1_s3), .A1(binary_to_bcd_main_2_s3), .A0(binary_to_bcd_main_3_s3),
    .S3(P9), .S2(binary_to_bcd_main_6_s2), .S1(binary_to_bcd_main_6_s1), .S0(binary_to_bcd_main_6_s0));
  binary_to_BCD_main binary_to_bcd_main_7 (
    .A3(binary_to_bcd_main_6_s2), .A2(binary_to_bcd_main_6_s1), .A1(binary_to_bcd_main_6_s0),
    .A0(binary_to_bcd_main_5_s3), .S3(P8), .S2(P7), .S1(P6), .S0(P5));

  assign P0 = B0;
endmodule

module BCD_to_seven_segment (
  input  A,
  input  B,
  input  C,
  input  D,
  output a_2,
  output b_2,
  output c_2,
  output d_2,
  output e,
  output f,
  output g
);

  wire and_1_out, and_2_out, and_3_out, and_4_out, and_5_out, and_6_out, and_7_out, and_8_out, and_9_out,
       not_1_out, not_2_out, not_3_out, not_4_out, or_1_out, or_4_out, or_5_out, or_6_out, or_7_out,
       or_8_out, or_9_out, or_10_out, or_13_out, or_14_out, or_15_out;

  not not_1 (not_1_out, A);
  not not_2 (not_2_out, B);
  not not_3 (not_3_out, C);
  not not_4 (not_4_out, D);
  and and_1 (and_1_out, B, D);
  and and_2 (and_2_out, not_2_out, not_4_out);
  and and_3 (and_3_out, C, D);
  and and_4 (and_4_out, not_3_out, not_4_out);
  or or_1 (or_1_out, B, not_3_out);
  and and_5 (and_5_out, C, not_4_out);
  and and_6 (and_6_out, not_2_out, C);
  and and_7 (and_7_out, B, not_3_out);
  and and_8 (and_8_out, B, not_4_out);
  and and_9 (and_9_out, D, and_7_out);
  or or_2 (c_2, or_1_out, D);
  or or_3 (e, and_2_out, and_5_out);
  or or_4 (or_4_out, A, C);
  or or_5 (or_5_out, A, and_2_out);
  or or_6 (or_6_out, and_2_out, or_4_out);
  or or_7 (or_7_out, and_3_out, and_4_out);
  or or_8 (or_8_out, or_5_out, and_5_out);
  or or_9 (or_9_out, and_4_out, and_8_out);
  or or_10 (or_10_out, A, and_7_out);
  or or_11 (a_2, and_1_out, or_6_out);
  or or_12 (b_2, or_7_out, not_2_out);
  or or_13 (or_13_out, or_8_out, and_6_out);
  or or_14 (or_14_out, or_9_out, and_7_out);
  or or_15 (or_15_out, and_5_out, or_10_out);
  or or_16 (d_2, or_13_out, and_9_out);
  or or_17 (f, or_14_out, A);
  or or_18 (g, and_6_out, or_15_out);
endmodule

// MUX
module _2___1_MUX_south (
  input  in_1,
  input  in_2,
  input  in_3,
  output out_4
);

  wire nand_1_out, nand_2_out, nand_4_out;

  nand nand_1 (nand_1_out, in_3, in_3);
  nand nand_2 (nand_2_out, nand_1_out, in_1);
  nand nand_3 (out_4, nand_2_out, nand_4_out);
  nand nand_4 (nand_4_out, in_3, in_2);
endmodule

module _4___1_MUX (
  input  in_1,
  input  in_2,
  input  in_3,
  input  in_4,
  input  in_5,
  input  in_6,
  output out_7
);

  wire nand_1_out, nand_2_out, nand_3_out, nand_4_out, nand_5_out, nand_6_out, nand_7_out, nand_8_out,
       nand_9_out, nand_10_out, nand_11_out, nand_12_out, nand_14_out, nand_15_out, nand_16_out, nand_17_out,
       nand_18_out, nand_19_out;

  nand nand_1 (nand_1_out, in_5, in_5);
  nand nand_2 (nand_2_out, in_6, in_6);
  nand nand_3 (nand_3_out, nand_2_out, in_1);
  nand nand_4 (nand_4_out, nand_3_out, nand_3_out);
  nand nand_5 (nand_5_out, nand_1_out, nand_4_out);
  nand nand_6 (nand_6_out, in_6, nand_10_out);
  nand nand_7 (nand_7_out, nand_5_out, nand_6_out);
  nand nand_8 (nand_8_out, nand_7_out, nand_7_out);
  nand nand_9 (nand_9_out, nand_1_out, in_2);
  nand nand_10 (nand_10_out, nand_9_out, nand_9_out);
  nand nand_11 (nand_11_out, nand_16_out, nand_19_out);
  nand nand_12 (nand_12_out, nand_11_out, nand_11_out);
  nand nand_13 (out_7, nand_8_out, nand_12_out);
  nand nand_14 (nand_14_out, nand_2_out, in_3);
  nand nand_15 (nand_15_out, nand_14_out, nand_14_out);
  nand nand_16 (nand_16_out, in_5, nand_15_out);
  nand nand_17 (nand_17_out, in_5, in_4);
  nand nand_18 (nand_18_out, nand_17_out, nand_17_out);
  nand nand_19 (nand_19_out, in_6, nand_18_out);
endmodule

module _2___1_MUX_east (
  input  in_1,
  input  in_2,
  input  in_3,
  output out_4
);

  wire nand_1_out, nand_2_out, nand_3_out;

  nand nand_1 (nand_1_out, in_3, in_3);
  nand nand_2 (nand_2_out, in_1, nand_1_out);
  nand nand_3 (nand_3_out, in_2, in_3);
  nand nand_4 (out_4, nand_2_out, nand_3_out);
endmodule

// DEMUX
module _4___1_DEMUX (
  input  in_1,
  input  in_2,
  input  in_3,
  output out_4,
  output out_5,
  output out_6,
  output out_7
);

  wire and_1_out, and_3_out, and_5_out, and_7_out, not_1_out, not_2_out;

  not not_1 (not_1_out, in_2);
  not not_2 (not_2_out, in_3);
  and and_1 (and_1_out, not_1_out, in_1);
  and and_2 (out_4, not_2_out, and_1_out);
  and and_3 (and_3_out, not_2_out, in_1);
  and and_4 (out_5, in_2, and_3_out);
  and and_5 (and_5_out, in_3, in_1);
  and and_6 (out_6, not_1_out, and_5_out);
  and and_7 (and_7_out, in_3, in_1);
  and and_8 (out_7, in_2, and_7_out);
endmodule
